# Fritzing sketch circuit (saved by Fritzing 0.9.3b)
breadboards: 1

parts:
  MH-ET_LIVE_ESP32_DEVKIT1 = MH-ET LIVE ESP32 DEVKIT 38 pins
  J1 = 120V duplex outlet_1
  HLK-PM1 = HLK-PM01
  relay = KY-019 5V Relay Module [package="Breakout board"]
  Mod1 = zmpt101b
  Part1 = LCD1602-I2C
  Part2 = ACS712 Current Sensor 5A 20A 30A

nets:
  N1: MH-ET_LIVE_ESP32_DEVKIT1.IO35, Part2.2, Part2.OUT
  N2: MH-ET_LIVE_ESP32_DEVKIT1.IO32, Mod1.OUT
  N3: MH-ET_LIVE_ESP32_DEVKIT1.GND#58, HLK-PM1.-Vo
  VCC: MH-ET_LIVE_ESP32_DEVKIT1.5V, HLK-PM1.+Vo, relay.+, Mod1.VCC, Part1.VCC, Part2.VCC
  GND: MH-ET_LIVE_ESP32_DEVKIT1.GND#64, J1.G, relay.-, Mod1.GND, Part1.GND, Part2.GND
  N4: MH-ET_LIVE_ESP32_DEVKIT1.IO23, Part1.SCL
  N5: MH-ET_LIVE_ESP32_DEVKIT1.IO21, Part1.SDA
  N6: MH-ET_LIVE_ESP32_DEVKIT1.IO19, relay.S
  N7: J1.H1, relay.Common, Mod1.L
  N8: J1.H2, HLK-PM1.AC#0
  N9: J1.N2, HLK-PM1.AC#1
  N10: relay.NC, Part2.1
  N11: relay.NO, Mod1.N

custom parts:
  MH-ET LIVE ESP32 DEVKIT 38 pins: http://mh.nodebb.com/topic/2/mh-et-live-esp32-devkit
  120V duplex outlet_1: 120V duplex outlet.
  HLK-PM01: AC-DC 220V to 5V Step-Down Power Supply Module
  KY-019 5V Relay Module: KY-019 5V Relay module, used to control AC circuits. (Special thanks to vanepp for fixing the PCB holes and other errors)
  zmpt101b: Single phase ac active output voltate transformer module.
  LCD1602-I2C: A standard character display, usually with 2x16 characters. Comes in many colors with LCM1602 IIC attached.
  ACS712 Current Sensor 5A 20A 30A: Remix by Michael Kubina http://www.kubina.info Original by: https://forum.fritzing.org/t/current-sensor-5a-acs712/7694 https://forum.fritzing.org/u/ArtHome ArtHome12@gmail.com
